# Fritzing sketch wireing_diagram (saved by Fritzing 0.9.3b)
breadboards: 1

parts:
  IC1 = MCP3008 8-channel 10-bit ADC [part_number=MCP3008]
  Raspberry_Pi_1 = Raspberry Pi 3 [part_number=RPI-3-V1.2]
  R1 = PHOTOCELL [package=photocell]
  LED1 = LED - 5mm [color="Red (633nm)" package="5 mm [THT]"]
  R2 = Resistor [tolerance=±5% resistance=220 package="2010 [SMD]"]
  R3 = Resistor [tolerance=±5% resistance=220 package="2010 [SMD]"]

nets:
  N1: IC1.no_name_yet#1, R1.P$2, R3.Pin_1
  N2: IC1.no_name_yet#9, IC1.no_name_yet#14, Raspberry_Pi_1.GND, LED1.cathode, R3.Pin_0
  N3: IC1.no_name_yet#10, Raspberry_Pi_1.GIPO18
  N4: IC1.no_name_yet#11, Raspberry_Pi_1.GIPO23
  N5: IC1.no_name_yet#12, Raspberry_Pi_1.GIPO24
  N6: IC1.no_name_yet#13, Raspberry_Pi_1.GIPO25
  3V3: IC1.no_name_yet#15, IC1.no_name_yet#16, Raspberry_Pi_1.3v3, Raspberry_Pi_1.3V3, R1.P$1
  N7: Raspberry_Pi_1.GIPO16, R2.Pin_0
  N8: LED1.anode, R2.Pin_1
